# Fritzing sketch Schema (saved by Fritzing 0.9.9b)
breadboards: 2

parts:
  Load_Cell1 = Load Cell - Red/white/black/green
  HC-SR04_Sensor_1 = HC-SR04 Ultrasonic Distance Sensor
  Mod1 = L298N DC motor driver
  Arduino_Uno = Arduino Uno (Rev3) - ICSP
  M1 = gear-motor
  LL = KY-033 Tracing Black White Line Hunting Sensor Module For Arduino
  L = KY-033 Tracing Black White Line Hunting Sensor Module For Arduino
  RR = KY-033 Tracing Black White Line Hunting Sensor Module For Arduino
  R = KY-033 Tracing Black White Line Hunting Sensor Module For Arduino
  M2 = gear-motor
  7_5V = 4 x AAA Battery Mount
  Interruttore = Pushbutton [package="[THT]"]
  R1 = Resistor [tolerance=±5% power=0.25 resistance=1k package=THT]
  LED2 = LED - 5mm [color="Red (633nm)" current=0.030 package="5 mm [THT]"]
  Componente1 = HX711 Weighing Sensor Module
  SG1 = Buzzer 12mm [package=buzzer-12mm-ns]

nets:
  N1: Load_Cell1.wire1, Componente1.E+
  N2: Load_Cell1.wire2, Componente1.A-
  N3: Load_Cell1.wire3, Componente1.E-
  N4: Load_Cell1.wire4, Componente1.A+
  VCC: HC-SR04_Sensor_1.VCC, Mod1.5V, Mod1.+5V-J1, Mod1.+5V-J2, Mod1.IN1, Mod1.IN3, Arduino_Uno.VIN, LL.V+, L.V+, RR.V+, R.V+, Componente1.VCC
  N5: HC-SR04_Sensor_1.TRIG, Arduino_Uno.D13/SCK
  N6: HC-SR04_Sensor_1.ECHO, Arduino_Uno.D12/MISO
  GND: HC-SR04_Sensor_1.GND, Mod1.GND, Mod1.IN2, Mod1.IN4, Arduino_Uno.GND, LL.GND, L.GND, RR.GND, R.GND, 7_5V.-, Interruttore.Pin_4, LED2.cathode, Componente1.GND, SG1.2
  N7: Mod1.OUT1, M2.pin_2
  N8: Mod1.OUT2, M2.pin_1
  N9: Mod1.12V, Mod1.5V-ENA-JMP-I, Mod1.5V-ENA-JMP-O, 7_5V.+
  N10: Mod1.OUT3, M1.pin_2
  N11: Mod1.OUT4, M1.pin_1
  N12: Mod1.ENA, Arduino_Uno.D6_PWM
  N13: Mod1.ENB, Arduino_Uno.D5_PWM
  N14: Arduino_Uno.A2, LL.S
  N15: Arduino_Uno.A3, L.S
  N16: Arduino_Uno.A4/SDA, R.S
  N17: Arduino_Uno.A5/SCL, RR.S
  N18: Arduino_Uno.D10_PWM/SS, SG1.1
  N19: Arduino_Uno.D11_PWM/MOSI, R1.Pin_0
  N20: Arduino_Uno.D2, Componente1.DT
  N21: Arduino_Uno.D3_PWM, Componente1.CK
  N22: Arduino_Uno.D4, Interruttore.Pin_1, Interruttore.Pin_2
  N23: R1.Pin_1, LED2.anode

custom parts:
  Load Cell - Red/white/black/green: A rectangle load cell/weighting pressure Sensor with four wires - Red, white, black, green. Normally corresponding with E+, E-, A+, A- respectively.
  L298N DC motor driver: 2x DC motor driver with 78M05 positive voltage regulator (7..35 V) L298N: max 46 V, 2 A Set 5 V Enable jumper to enable 5 V regultor (needed for the L298N) and +5 V output at screw terminal or supply external +5 V at screw terminal Set ENA and/or ENB to +5 V to enable motor permanently or supply ENA and/or ENB with PWM signal IN1 and IN2 set rotation directory for motor A (OUT1/OUT2) IN2 and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
  KY-033 Tracing Black White Line Hunting Sensor Module For Arduino: Tracing Black White Line Hunting Sensor Module For Arduino Description: This is KY-033 tracking sensor. The KY-033 measures the intensity of infrared radiation and delivers it as an analog output voltage. Features: Operating voltage: 2.5 - 12V(cannot over12V) working current: 18mA-20mA at 5V Enhanced accuracy Documents: http://www.vishay.com/docs/83760/tcrt5000.pdf
  HX711 Weighing Sensor Module: HX711 is a precision 24-bit analog-to-digital converter (ADC) designed for weigh scales and industrial control applications to interface directly with a bridge sensor.
